// Logisim project ALU.circ as structural Verilog: 3 circuits, main circuit ALU
module ALU (
  input  [31:0] A,
  input  [31:0] B,
  input  [4:0] Shift,
  input  CarryIn,
  input  [3:0] Codop,
  output [3:0] Flags,
  output [31:0] S
);

  wire adder_1_cout, adder_4_cout, bitselector_1_out, bitselector_2_out, bitselector_3_out,
       bitselector_4_out, bitselector_5_out, bitselector_6_out, bitselector_7_out, bitselector_8_out,
       bitselector_9_out, bitselector_10_out, bitselector_11_out, bitselector_12_out, bitselector_13_out,
       bitselector_14_out, bitselector_15_out, not_3_out, v_add_1_v, v_add_2_v, v_sub_1_v, v_sub_2_v;
  wire [4:0] subtractor_2_out, subtractor_3_out;
  wire [31:0] ADC, adder_2_out, and_1_out, and_2_out, and_3_out, CMN, CMP, multiplexer_2_out,
       multiplier_1_out, negator_1_out, negator_2_out, negator_3_out, not_1_out, not_2_out, or_1_out, SBC,
       shifter_1_out, shifter_2_out, shifter_3_out, shifter_4_out, xor_1_out;

  assign and_1_out = A & B;  // AND_Gate and_1, 32 bits wide
  assign xor_1_out = A ^ B;  // XOR_Gate xor_1, 32 bits wide
  Shifter #(.width(32)) shifter_1 (.in(B), .\dist (Shift), .out(shifter_1_out));
  Shifter #(.width(32), .shift("lr")) shifter_2 (.in(B), .\dist (Shift), .out(shifter_2_out));
  Shifter #(.width(32), .shift("ar")) shifter_3 (.in(B), .\dist (Shift), .out(shifter_3_out));
  Adder #(.width(32)) adder_1 (.a(A), .b(B), .out(ADC), .cin(CarryIn), .cout(adder_1_cout));
  Adder #(.width(32)) adder_2 (.a(A), .b(negator_1_out), .out(adder_2_out), .cin(CarryIn));  // open: cout
  Negator #(.width(32)) negator_1 (.in(B), .out(negator_1_out));
  Negator #(.width(32)) negator_2 (.in(32'h1), .out(negator_2_out));
  Shifter #(.width(32), .shift("rr")) shifter_4 (.in(B), .\dist (Shift), .out(shifter_4_out));
  assign and_2_out = A & B;  // AND_Gate and_2, 32 bits wide
  Negator #(.width(32)) negator_3 (.in(A), .out(negator_3_out));
  Subtractor #(.width(32)) subtractor_1 (.a(A), .b(B), .out(CMP));  // open: bin, bout
  Adder #(.width(32)) adder_3 (.a(A), .b(B), .out(CMN));  // open: cin, cout
  assign or_1_out = A | B;  // OR_Gate or_1, 32 bits wide
  Multiplier #(.width(32)) multiplier_1 (.a(A), .b(B), .out(multiplier_1_out));  // open: cin, cout
  assign not_1_out = ~B;  // NOT_Gate not_1, 32 bits wide
  assign not_2_out = ~B;  // NOT_Gate not_2, 32 bits wide
  Adder #(.width(32)) adder_4 (.a(adder_2_out), .b(negator_2_out), .out(SBC), .cout(adder_4_cout));  // open: cin
  not not_3 (not_3_out, adder_4_cout);
  assign and_3_out = A & not_1_out;  // AND_Gate and_3, 32 bits wide
  Multiplexer #(.select(4), .width(32), .enable("false")) multiplexer_1 (
    .in0(and_1_out), .in1(xor_1_out), .in2(shifter_1_out), .in3(shifter_2_out), .in4(shifter_3_out),
    .in5(ADC), .in6(SBC), .in7(shifter_4_out), .in8(B), .in9(negator_3_out), .in10(B), .in11(B),
    .in12(or_1_out), .in13(multiplier_1_out), .in14(and_3_out), .in15(not_2_out), .out(S), .sel(Codop));
  Multiplexer #(.select(4), .width(32), .enable("false")) multiplexer_2 (
    .in0(and_1_out), .in1(xor_1_out), .in2(shifter_1_out), .in3(shifter_2_out), .in4(shifter_3_out),
    .in5(ADC), .in6(SBC), .in7(shifter_4_out), .in8(and_2_out), .in9(negator_3_out), .in10(CMP), .in11(CMN),
    .in12(or_1_out), .in13(multiplier_1_out), .in14(and_3_out), .in15(not_2_out), .out(multiplexer_2_out),
    .sel(Codop));
  Comparator #(.width(32)) comparator_1 (
    .a(multiplexer_2_out), .b({32{1'b0}}), .eq(Flags[2]), .lt(Flags[3]));  // open: gt
  BitSelector #(.width(32)) bitselector_1 (.in(shifter_4_out), .out(bitselector_1_out), .sel({5{1'b1}}));
  Multiplexer #(.select(4), .enable("false")) multiplexer_3 (
    .in0(1'b0), .in1(1'b0), .in2(bitselector_2_out), .in3(bitselector_3_out), .in4(bitselector_3_out),
    .in5(adder_1_cout), .in6(not_3_out), .in7(bitselector_1_out), .in8(1'b0), .in9(1'b0), .in10(1'b0),
    .in11(1'b0), .in12(1'b0), .in13(1'b0), .in14(1'b0), .in15(1'b0), .out(Flags[1]), .sel(Codop));
  Subtractor #(.width(5)) subtractor_2 (.a({5{1'b0}}), .b(Shift), .out(subtractor_2_out));  // open: bin, bout
  BitSelector #(.width(32)) bitselector_2 (.in(B), .out(bitselector_2_out), .sel(subtractor_2_out));
  Subtractor #(.width(5)) subtractor_3 (.a(Shift), .b(5'b00001), .out(subtractor_3_out));  // open: bin, bout
  BitSelector #(.width(32)) bitselector_3 (.in(B), .out(bitselector_3_out), .sel(subtractor_3_out));
  BitSelector #(.width(32)) bitselector_4 (.in(ADC), .out(bitselector_4_out), .sel({5{1'b1}}));
  BitSelector #(.width(32)) bitselector_5 (.in(A), .out(bitselector_5_out), .sel({5{1'b1}}));
  BitSelector #(.width(32)) bitselector_6 (.in(B), .out(bitselector_6_out), .sel({5{1'b1}}));
  V_add v_add_1 (.A(bitselector_5_out), .B(bitselector_6_out), .S(bitselector_4_out), .V(v_add_1_v));
  BitSelector #(.width(32)) bitselector_7 (.in(SBC), .out(bitselector_7_out), .sel({5{1'b1}}));
  BitSelector #(.width(32)) bitselector_8 (.in(B), .out(bitselector_8_out), .sel({5{1'b1}}));
  Multiplexer #(.select(4), .enable("false")) multiplexer_4 (
    .in0(1'b0), .in1(1'b0), .in2(1'b0), .in3(1'b0), .in4(1'b0), .in5(v_add_1_v), .in6(v_sub_1_v), .in7(1'b0),
    .in8(1'b0), .in9(1'b0), .in10(v_sub_2_v), .in11(v_add_2_v), .in12(1'b0), .in13(1'b0), .in14(1'b0),
    .in15(1'b0), .out(Flags[0]), .sel(Codop));
  BitSelector #(.width(32)) bitselector_9 (.in(A), .out(bitselector_9_out), .sel({5{1'b1}}));
  V_sub v_sub_1 (.A(bitselector_9_out), .B(bitselector_8_out), .S(bitselector_7_out), .V(v_sub_1_v));
  BitSelector #(.width(32)) bitselector_10 (.in(CMP), .out(bitselector_10_out), .sel({5{1'b1}}));
  BitSelector #(.width(32)) bitselector_11 (.in(A), .out(bitselector_11_out), .sel({5{1'b1}}));
  BitSelector #(.width(32)) bitselector_12 (.in(B), .out(bitselector_12_out), .sel({5{1'b1}}));
  V_sub v_sub_2 (.A(bitselector_11_out), .B(bitselector_12_out), .S(bitselector_10_out), .V(v_sub_2_v));
  BitSelector #(.width(32)) bitselector_13 (.in(CMN), .out(bitselector_13_out), .sel({5{1'b1}}));
  BitSelector #(.width(32)) bitselector_14 (.in(A), .out(bitselector_14_out), .sel({5{1'b1}}));
  BitSelector #(.width(32)) bitselector_15 (.in(B), .out(bitselector_15_out), .sel({5{1'b1}}));
  V_add v_add_2 (.A(bitselector_14_out), .B(bitselector_15_out), .S(bitselector_13_out), .V(v_add_2_v));

  // Other names for the same wires on the sheet: V = Flags[0]; C = Flags[1]; Z = Flags[2]; N = Flags[3]

  // Notes on the sheet:
  //   Note: for ROR, C = N
  //   Note 2: assume that shift > 0 for LSL and LSR
endmodule

module V_add (
  input  A,
  input  B,
  input  S,
  output V
);

  wire and_1_out, and_2_out, not_1_out, not_2_out, not_3_out;

  not not_1 (not_1_out, A);
  not not_2 (not_2_out, B);
  not not_3 (not_3_out, S);
  and and_1 (and_1_out, not_1_out, not_2_out, S);
  or or_1 (V, and_1_out, and_2_out);
  and and_2 (and_2_out, A, B, not_3_out);
endmodule

module V_sub (
  input  A,
  input  B,
  input  S,
  output V
);

  wire and_1_out, and_2_out, not_1_out, not_2_out, not_3_out;

  not not_1 (not_1_out, A);
  not not_2 (not_2_out, B);
  not not_3 (not_3_out, S);
  and and_1 (and_1_out, not_1_out, B, S);
  or or_1 (V, and_1_out, and_2_out);
  and and_2 (and_2_out, A, not_2_out, not_3_out);
endmodule
