// Logisim project Controller.circ as structural Verilog: 13 circuits, main circuit Controller
module Controller (
  input  [15:0] Inst,
  input  [3:0] Flags,
  input  Clk,
  input  Reset,
  output Carry,
  output DP_Shift,
  output Imm32_Enable,
  output [4:0] Imm5,
  output [31:0] Imm32,
  output [3:0] ALU_Opcode,
  output [2:0] Rm,
  output [2:0] Rn,
  output [2:0] Rd,
  output [31:0] RAM_Addr,
  output Load,
  output Store,
  output [7:0] PC
);

  wire Conditional_1_verified, Load_Store_1_pc_hold, not_1_out, Opcode_Decoder_1_conditional,
       Opcode_Decoder_1_data_processing, Opcode_Decoder_1_load_store, Opcode_Decoder_1_shift,
       Opcode_Decoder_1_sp_address, Shift_Add_Sub_Mov_1_carry, SP_Address_1_write_enable;
  wire [2:0] Data_Processing_1_rd, Data_Processing_1_rm, Data_Processing_1_rn, Load_Store_1_rd,
       Load_Store_1_rm, Shift_Add_Sub_Mov_1_rd, Shift_Add_Sub_Mov_1_rm, Shift_Add_Sub_Mov_1_rn;
  wire [3:0] Data_Processing_1_alu_opcode, Data_Processing_1_flags_update_mask, flags_apsr_1_flags_out,
       or_1_out, Shift_Add_Sub_Mov_1_alu_opcode, Shift_Add_Sub_Mov_1_flags_update_mask;
  wire [7:0] adder_1_out, adder_2_out, Conditional_1_offset;
  wire [31:0] SP_Address_1_new_stack_pointer, Stack_Pointer_q;

  Register #(.width(32)) Stack_Pointer (
    .D(SP_Address_1_new_stack_pointer), .en(SP_Address_1_write_enable), .clk(Clk), .Q(Stack_Pointer_q),
    .clr(Reset));
  Opcode_Decoder Opcode_Decoder_1 (
    .Opcode(Inst[15:10]), .Shift(Opcode_Decoder_1_shift), .Data_Processing(Opcode_Decoder_1_data_processing),
    .Load_Store(Opcode_Decoder_1_load_store), .SP_Address(Opcode_Decoder_1_sp_address),
    .Conditional(Opcode_Decoder_1_conditional));
  assign or_1_out = Data_Processing_1_flags_update_mask | Shift_Add_Sub_Mov_1_flags_update_mask;  // OR_Gate or_1, 4 bits wide
  Shift_Add_Sub_Mov Shift_Add_Sub_Mov_1 (
    .Imm32_Enable(Imm32_Enable), .Instruction(Inst), .ALU_Opcode(Shift_Add_Sub_Mov_1_alu_opcode),
    .Enable(Opcode_Decoder_1_shift), .Carry(Shift_Add_Sub_Mov_1_carry),
    .Flags_Update_Mask(Shift_Add_Sub_Mov_1_flags_update_mask), .Rd(Shift_Add_Sub_Mov_1_rd),
    .Rn(Shift_Add_Sub_Mov_1_rn), .Rm(Shift_Add_Sub_Mov_1_rm), .Imm5(Imm5), .Imm32(Imm32));
  Data_Processing Data_Processing_1 (
    .Instruction(Inst), .ALU_Opcode(Data_Processing_1_alu_opcode), .Enable(Opcode_Decoder_1_data_processing),
    .Rm(Data_Processing_1_rm), .Rn(Data_Processing_1_rn), .Rd(Data_Processing_1_rd),
    .Flags_Update_Mask(Data_Processing_1_flags_update_mask));
  Flags_APSR flags_apsr_1 (
    .Flags_In(or_1_out), .Update_Mask(Flags), .Clk(Clk), .Rst(Reset), .Flags_Out(flags_apsr_1_flags_out));
  Load_Store Load_Store_1 (
    .Store(Store), .Rm(Load_Store_1_rm), .Stack_Pointer(Stack_Pointer_q), .Instruction(Inst),
    .RAM_Addr(RAM_Addr), .Rd(Load_Store_1_rd), .Enable(Opcode_Decoder_1_load_store), .Load(Load), .Clk(Clk),
    .Reset(Reset), .PC_Hold(Load_Store_1_pc_hold));
  Conditional Conditional_1 (
    .Offset(Conditional_1_offset), .Instruction(Inst), .Enable(Opcode_Decoder_1_conditional),
    .Verified(Conditional_1_verified), .Z(flags_apsr_1_flags_out[2]), .V(flags_apsr_1_flags_out[0]),
    .C(flags_apsr_1_flags_out[1]), .N(flags_apsr_1_flags_out[3]));
  SP_Address SP_Address_1 (
    .New_Stack_Pointer(SP_Address_1_new_stack_pointer), .Write_Enable(SP_Address_1_write_enable),
    .Stack_Pointer(Stack_Pointer_q), .Enable(Opcode_Decoder_1_sp_address), .Instruction(Inst));
  Adder adder_1 (.a(8'h3), .b(Conditional_1_offset), .out(adder_1_out), .cin(1'b0));  // open: cout
  Adder adder_2 (.a(adder_1_out), .b(PC), .out(adder_2_out), .cin(1'b0));  // open: cout
  and and_1 (DP_Shift, Opcode_Decoder_1_shift, ~Opcode_Decoder_1_data_processing);  // AND_Gate
  not not_1 (not_1_out, Load_Store_1_pc_hold);
  Counter counter_1 (
    .clr(Reset), .load(Conditional_1_verified), .up(1'b1), .count(not_1_out), .clk(Clk), .D(adder_2_out),
    .Q(PC));  // open: carry
  Multiplexer #(.enable("false")) multiplexer_1 (
    .in0(flags_apsr_1_flags_out[1]), .in1(Shift_Add_Sub_Mov_1_carry), .out(Carry), .sel(DP_Shift));
  assign ALU_Opcode = Shift_Add_Sub_Mov_1_alu_opcode | Data_Processing_1_alu_opcode;  // OR_Gate or_2, 4 bits wide
  assign Rm = Shift_Add_Sub_Mov_1_rm | Data_Processing_1_rm | Load_Store_1_rm;  // OR_Gate or_3, 3 bits wide
  assign Rn = Shift_Add_Sub_Mov_1_rn | Data_Processing_1_rn;  // OR_Gate or_4, 3 bits wide
  assign Rd = Shift_Add_Sub_Mov_1_rd | Data_Processing_1_rd | Load_Store_1_rd;  // OR_Gate or_5, 3 bits wide

  // Notes on the sheet:
  //   Extract carry
  //   Extract Opcode
  //   IF Reg_Imm=1 THEN use shift value from register ELSE use shift value from Imm5
  //   Buffer flags for next instruction
  //   Add 3 to offset because ARM pre-increments PC
  //   and does an additionnal prefect operation
endmodule

module Conditional (
  input  Enable,
  input  [15:0] Instruction,
  input  Z,
  input  C,
  input  N,
  input  V,
  output [7:0] Offset,
  output Verified
);

  wire and_1_out, and_2_out, and_3_out, multiplexer_2_out, not_1_out, not_2_out, not_3_out, not_4_out,
       not_5_out, not_6_out, not_7_out, or_1_out, xnor_1_out, xor_1_out, xor_2_out;
  wire [3:0] selec;
  wire [7:0] bitselector_2_out;

  BitSelector #(.width(16), .group(4)) bitselector_1 (.in(Instruction), .out(selec), .sel(2'b10));
  and and_1 (and_1_out, C, not_1_out);
  not not_1 (not_1_out, Z);
  not not_2 (not_2_out, C);
  and and_2 (and_2_out, not_2_out, Z);
  xor xor_1 (xor_1_out, N, V);
  xnor xnor_1 (xnor_1_out, N, V);
  not not_3 (not_3_out, Z);
  xor xor_2 (xor_2_out, V, Z);
  BitSelector #(.width(16), .group(8)) bitselector_2 (.in(Instruction), .out(bitselector_2_out), .sel(1'b0));
  not not_4 (not_4_out, Z);
  not not_5 (not_5_out, C);
  not not_6 (not_6_out, N);
  not not_7 (not_7_out, V);
  and and_3 (and_3_out, xnor_1_out, not_3_out);
  or or_1 (or_1_out, xor_2_out, Z);
  Multiplexer #(.width(8), .enable("false")) multiplexer_1 (
    .in0({8{1'b0}}), .in1(bitselector_2_out), .out(Offset), .sel(Enable));
  Multiplexer #(.select(4), .enable("false")) multiplexer_2 (
    .in0(Z), .in1(not_4_out), .in2(C), .in3(not_5_out), .in4(N), .in5(not_6_out), .in6(V), .in7(not_7_out),
    .in8(and_1_out), .in9(and_2_out), .in10(xnor_1_out), .in11(xor_1_out), .in12(and_3_out), .in13(or_1_out),
    .in14(1'b1), .out(multiplexer_2_out), .sel(selec));  // open: in15
  Multiplexer #(.enable("false")) multiplexer_3 (.in0(1'b0), .in1(multiplexer_2_out), .out(Verified), .sel(Enable));
endmodule

module Opcode_Decoder (
  input  [5:0] Opcode,
  output Shift,
  output Data_Processing,
  output Load_Store,
  output SP_Address,
  output Conditional
);

  wire not_1_out, not_2_out, not_3_out;

  not not_1 (not_1_out, Opcode[5]);
  nor nor_1 (Shift, Opcode[4], Opcode[5]);
  not not_2 (not_2_out, Opcode[3]);
  not not_3 (not_3_out, Opcode[4]);
  and and_1 (Data_Processing, Opcode[4], not_1_out);
  and and_2 (Load_Store, not_2_out, not_3_out, Opcode[5], Opcode[2]);
  and and_3 (SP_Address, not_3_out, Opcode[3], Opcode[5], Opcode[2]);
  and and_4 (Conditional, Opcode[5], Opcode[4]);

  // Notes on the sheet:
  //   Shift, add, sub, mov
  //   Load/Store
  //   SP Address
  //   Data Processing
  //   Conditional branch
endmodule

module Data_Processing (
  input  [15:0] Instruction,
  input  Enable,
  output [2:0] Rn,
  output [2:0] Rd,
  output [2:0] Rm,
  output [3:0] ALU_Opcode,
  output [3:0] Flags_Update_Mask
);

  wire [2:0] bitundeuxtrois, Rd_t, RM_t, Rn_t;
  wire [3:0] flags, opcode;
  wire [5:0] bitselector_1_out;

  BitSelector #(.width(16), .group(6)) bitselector_1 (.in(Instruction), .out(bitselector_1_out), .sel(2'b01));
  BitSelector #(.width(16), .group(3)) bitselector_2 (.in(Instruction), .out(bitundeuxtrois), .sel(3'b000));
  BitSelector #(.width(16), .group(3)) bitselector_3 (.in(Instruction), .out(RM_t), .sel(3'b001));
  BitSelector #(.width(6), .group(4)) bitselector_4 (.in(bitselector_1_out), .out(opcode), .sel(1'b0));
  Multiplexer #(.select(4), .width(4), .enable("false")) multiplexer_1 (
    .in0(4'b1110), .in1(4'b1110), .in2(4'b1110), .in3(4'b1110), .in4(4'b1110), .in5(4'b1111), .in6(4'b1111),
    .in7(4'b1110), .in8(4'b1110), .in9(4'b1111), .in10(4'b1111), .in11(4'b1111), .in12(4'b1110),
    .in13(4'b1100), .in14(4'b1110), .in15(4'b1110), .out(flags), .sel(opcode));
  Multiplexer #(.select(4), .width(3), .enable("false")) multiplexer_2 (
    .in0(bitundeuxtrois), .in1(bitundeuxtrois), .in2(bitundeuxtrois), .in3(bitundeuxtrois),
    .in4(bitundeuxtrois), .in5(bitundeuxtrois), .in6(bitundeuxtrois), .in7(bitundeuxtrois),
    .in8(bitundeuxtrois), .in9(3'b000), .in10(bitundeuxtrois), .in11(bitundeuxtrois), .in12(bitundeuxtrois),
    .in13(3'b000), .in14(bitundeuxtrois), .in15(3'b000), .out(Rn_t), .sel(opcode));
  Multiplexer #(.width(3), .enable("false")) multiplexer_3 (.in0(3'b000), .in1(Rn_t), .out(Rn), .sel(Enable));
  Multiplexer #(.width(3), .enable("false")) multiplexer_4 (.in0(3'b000), .in1(Rd_t), .out(Rd), .sel(Enable));
  Multiplexer #(.width(3), .enable("false")) multiplexer_5 (.in0(3'b000), .in1(RM_t), .out(Rm), .sel(Enable));
  Multiplexer #(.width(4), .enable("false")) multiplexer_6 (
    .in0(4'b0000), .in1(opcode), .out(ALU_Opcode), .sel(Enable));
  Multiplexer #(.width(4), .enable("false")) multiplexer_7 (
    .in0(4'b0000), .in1(flags), .out(Flags_Update_Mask), .sel(Enable));
  Multiplexer #(.select(4), .width(3), .enable("false")) multiplexer_8 (
    .in0(bitundeuxtrois), .in1(bitundeuxtrois), .in2(bitundeuxtrois), .in3(bitundeuxtrois),
    .in4(bitundeuxtrois), .in5(bitundeuxtrois), .in6(bitundeuxtrois), .in7(bitundeuxtrois), .in8(3'b000),
    .in9(bitundeuxtrois), .in10(3'b000), .in11(3'b000), .in12(bitundeuxtrois), .in13(bitundeuxtrois),
    .in14(bitundeuxtrois), .in15(bitundeuxtrois), .out(Rd_t), .sel(opcode));

  // Other names for the same wires on the sheet: i[15:0] = Instruction

  // Notes on the sheet:
  //   Pull output low on Enable = 0
  //   Note 2: RSB instruction has Rn as 1st operand.
  //   MUL instruction has Rn as 1st operand and Rdm as 2nd operand
  //   For simplification purposes, Rm is used for 1st operand both here and in the ALU.
  //   Note: instructions that does not save the result will still have the second operand as the destination register, the ALU will copy the second register to the destination register
endmodule

module Shift_Add_Sub_Mov (
  input  Enable,
  input  [15:0] Instruction,
  output [2:0] Rm,
  output [4:0] Imm5,
  output Carry,
  output [2:0] Rn,
  output [2:0] Rd,
  output [31:0] Imm32,
  output Imm32_Enable,
  output [3:0] Flags_Update_Mask,
  output [3:0] ALU_Opcode
);

  wire addsub_imm_s, addsub_register_s, and_1_out, Carry1, mov, multiplexer_1_out, multiplexer_4_out,
       not_1_out, shift, xor_1_out;
  wire [1:0] dix_neuf;
  wire [2:0] bitselector_4_out, bitselector_7_out, bitselector_8_out, bitselector_9_out, bitselector_11_out,
       multiplexer_2_out, multiplexer_5_out, multiplexer_8_out, treize_douze_onze;
  wire [3:0] multiplexer_3_out, multiplexer_7_out, multiplexer_14_out;
  wire [4:0] bitselector_13_out, multiplexer_16_out;
  wire [5:0] bitselector_10_out;
  wire [7:0] bitselector_1_out, bitselector_12_out;
  wire [8:0] bitselector_5_out;
  wire [10:0] bitselector_2_out;
  wire [15:0] controlled_buffer_1_out, controlled_buffer_2_out;
  wire [31:0] bit_extender_1_out, bit_extender_2_out, multiplexer_6_out, multiplexer_11_out,
       multiplexer_17_out, negator_1_out;

  SUB sub_1 (.e13(Instruction[13]), .e12(Instruction[12]), .e11(Instruction[11]), .e9(Instruction[9]), .s(Carry1));
  BitSelector #(.width(16), .group(8)) bitselector_1 (.in(Instruction), .out(bitselector_1_out), .sel(1'b1));
  BitSelector #(.width(16), .group(11)) bitselector_2 (.in(Instruction), .out(bitselector_2_out), .sel(1'b1));
  BitSelector #(.width(11), .group(3)) bitselector_3 (.in(bitselector_2_out), .out(treize_douze_onze), .sel(2'b00));
  BitSelector #(.group(3)) bitselector_4 (.in(bitselector_1_out), .out(bitselector_4_out), .sel(2'b00));
  BitSelector #(.width(16), .group(9)) bitselector_5 (.in(Instruction), .out(bitselector_5_out), .sel(1'b1));
  BitSelector #(.width(9), .group(2)) bitselector_6 (.in(bitselector_5_out), .out(dix_neuf), .sel(3'b000));
  add_subR addsub_register (.e10(Instruction[10]), .e11(Instruction[11]), .e12(Instruction[12]), .s(addsub_register_s));
  shi_ft shi (.e11(Instruction[11]), .e12(Instruction[12]), .e13(Instruction[13]), .s(shift));
  BitSelector #(.width(16), .group(3)) bitselector_7 (.in(Instruction), .out(bitselector_7_out), .sel(3'b001));
  BitSelector #(.width(16), .group(3)) bitselector_8 (.in(Instruction), .out(bitselector_8_out), .sel(3'b000));
  assign controlled_buffer_1_out = addsub_imm_s ? Instruction : 16'bz;  // Controlled_Buffer controlled_buffer_1
  addsub_I addsub_imm (.e10(Instruction[10]), .e11(Instruction[11]), .e12(Instruction[12]), .s(addsub_imm_s));
  MOV mov_1 (.e11(Instruction[11]), .e12(Instruction[12]), .e13(Instruction[13]), .s(mov));
  and and_1 (and_1_out, Instruction[11], Instruction[12]);
  BitSelector #(.width(16), .group(3)) bitselector_9 (.in(Instruction), .out(bitselector_9_out), .sel(3'b010));
  BitSelector #(.width(16), .group(6)) bitselector_10 (.in(Instruction), .out(bitselector_10_out), .sel(2'b01));
  Multiplexer #(.enable("false")) multiplexer_1 (.in0(1'b0), .in1(shift), .out(multiplexer_1_out), .sel(shift));
  not not_1 (not_1_out, Instruction[13]);
  Multiplexer #(.width(3), .enable("false")) multiplexer_2 (
    .in0(bitselector_8_out), .in1(bitselector_4_out), .out(multiplexer_2_out), .sel(Instruction[13]));
  BitSelector #(.width(16), .group(3)) bitselector_11 (
    .in(controlled_buffer_1_out), .out(bitselector_11_out), .sel(3'b010));
  assign bit_extender_1_out = {{29{1'b0}}, bitselector_11_out};  // Bit_Extender bit_extender_1
  assign bit_extender_2_out = {{24{1'b0}}, bitselector_12_out};  // Bit_Extender bit_extender_2
  BitSelector #(.width(16), .group(8)) bitselector_12 (
    .in(controlled_buffer_2_out), .out(bitselector_12_out), .sel(1'b0));
  assign controlled_buffer_2_out = mov ? Instruction : 16'bz;  // Controlled_Buffer controlled_buffer_2
  xor xor_1 (xor_1_out, addsub_imm_s, mov);
  Multiplexer #(.width(4), .enable("false")) multiplexer_3 (
    .in0(4'b1110), .in1(4'b1111), .out(multiplexer_3_out), .sel(and_1_out));
  BitSelector #(.width(6), .group(5)) bitselector_13 (.in(bitselector_10_out), .out(bitselector_13_out), .sel(1'b0));
  Multiplexer #(.enable("false")) multiplexer_4 (
    .in0(multiplexer_1_out), .in1(1'b1), .out(multiplexer_4_out), .sel(Carry1));
  Multiplexer #(.width(3), .enable("false")) multiplexer_5 (
    .in0(3'b000), .in1(bitselector_7_out), .out(multiplexer_5_out), .sel(not_1_out));
  Multiplexer #(.width(32), .enable("false")) multiplexer_6 (
    .in0(bit_extender_1_out), .in1(bit_extender_2_out), .out(multiplexer_6_out), .sel(Instruction[13]));
  Multiplexer #(.width(4), .enable("false")) multiplexer_7 (
    .in0(multiplexer_3_out), .in1(4'b1100), .out(multiplexer_7_out), .sel(Instruction[13]));
  Multiplexer #(.width(3), .enable("false")) multiplexer_8 (
    .in0(3'b000), .in1(bitselector_9_out), .out(multiplexer_8_out), .sel(addsub_register_s));
  Multiplexer #(.enable("false")) multiplexer_9 (.in0(1'b0), .in1(multiplexer_4_out), .out(Carry), .sel(Enable));
  Multiplexer #(.width(3), .enable("false")) multiplexer_10 (
    .in0(3'b000), .in1(multiplexer_5_out), .out(Rn), .sel(Enable));
  Multiplexer #(.width(32), .enable("false")) multiplexer_11 (
    .in0({32{1'b0}}), .in1(multiplexer_6_out), .out(multiplexer_11_out), .sel(xor_1_out));
  Negator #(.width(32)) negator_1 (.in(multiplexer_11_out), .out(negator_1_out));
  Multiplexer #(.enable("false")) multiplexer_12 (.in0(1'b0), .in1(xor_1_out), .out(Imm32_Enable), .sel(Enable));
  Multiplexer #(.width(4), .enable("false")) multiplexer_13 (
    .in0(4'b0000), .in1(multiplexer_7_out), .out(Flags_Update_Mask), .sel(Enable));
  Multiplexer #(.select(2), .width(4), .enable("false")) multiplexer_14 (
    .in0(4'b0101), .in1(4'b0110), .in2(4'b0101), .in3(4'b0110), .out(multiplexer_14_out), .sel(dix_neuf));
  Multiplexer #(.width(3), .enable("false")) multiplexer_15 (
    .in0(3'b000), .in1(multiplexer_8_out), .out(Rm), .sel(Enable));
  Multiplexer #(.width(5), .enable("false")) multiplexer_16 (
    .in0({5{1'b0}}), .in1(bitselector_13_out), .out(multiplexer_16_out), .sel(shift));
  Multiplexer #(.width(32), .enable("false")) multiplexer_17 (
    .in0(multiplexer_11_out), .in1(negator_1_out), .out(multiplexer_17_out), .sel(mov));
  Multiplexer #(.select(3), .width(4), .enable("false")) multiplexer_18 (
    .in0(4'b0010), .in1(4'b0011), .in2(4'b0100), .in3(multiplexer_14_out), .in4(4'b1001), .in5(4'b0000),
    .in6(4'b0000), .in7(4'b0000), .out(ALU_Opcode), .sel(treize_douze_onze));
  Multiplexer #(.width(3), .enable("false")) multiplexer_19 (
    .in0(3'b000), .in1(multiplexer_2_out), .out(Rd), .sel(Enable));
  Multiplexer #(.width(5), .enable("false")) multiplexer_20 (
    .in0({5{1'b0}}), .in1(multiplexer_16_out), .out(Imm5), .sel(Enable));
  Multiplexer #(.width(32), .enable("false")) multiplexer_21 (
    .in0({32{1'b0}}), .in1(multiplexer_17_out), .out(Imm32), .sel(Enable));

  // Other names for the same wires on the sheet: i[15:0] = Instruction; e11 = Instruction[11]; e12 = Instruction[12];
  //   e13 = Instruction[13]

  // Notes on the sheet:
  //   Pull output low on Enable = 0
  //   Note 3: Imm32_Enable forces the use of the immediate for Rm register
  //   Enable carry for SUB since it is reversed in ALU
  //   ALU will use Imm32 instead of Rm
  //   Note: ALU uses Rn register for shifts. Use Rn instead of Rm for shifts (immediate) here too
  //   Note 2: MOV uses RSB ALU opcode with Imm8 reversed so that it is copied to output register
endmodule

module Load_Store (
  input  [15:0] Instruction,
  input  Enable,
  input  [31:0] Stack_Pointer,
  input  Reset,
  input  Clk,
  output [31:0] RAM_Addr,
  output Load,
  output PC_Hold,
  output [2:0] Rd,
  output [2:0] Rm,
  output Store
);

  wire and_1_out, d_ff_1_qn, pchold, store_t;
  wire [2:0] rt;
  wire [7:0] bitselector_1_out, bitselector_2_out;
  wire [31:0] bit_extender_1_out, ram_addr_t;

  D_Flip_Flop d_ff_1 (.D(and_1_out), .clk(Clk), .Q(pchold), .Qn(d_ff_1_qn), .reset(Reset));  // open: preset
  and and_1 (and_1_out, d_ff_1_qn, Instruction[11]);
  BitSelector #(.width(16), .group(8)) bitselector_1 (.in(Instruction), .out(bitselector_1_out), .sel(1'b0));
  BitSelector #(.width(16), .group(8)) bitselector_2 (.in(Instruction), .out(bitselector_2_out), .sel(1'b1));
  BitSelector #(.group(3)) bitselector_3 (.in(bitselector_2_out), .out(rt), .sel(2'b00));
  assign bit_extender_1_out = {{24{1'b0}}, bitselector_1_out};  // Bit_Extender bit_extender_1
  Adder #(.width(32)) adder_1 (.a(bit_extender_1_out), .b(Stack_Pointer), .out(ram_addr_t));  // open: cin, cout
  not not_1 (store_t, Instruction[11]);
  Multiplexer #(.width(32), .enable("false")) multiplexer_1 (
    .in0({32{1'b0}}), .in1(ram_addr_t), .out(RAM_Addr), .sel(Enable));
  Multiplexer #(.enable("false")) multiplexer_2 (.in0(1'b0), .in1(Instruction[11]), .out(Load), .sel(Enable));
  Multiplexer #(.enable("false")) multiplexer_3 (.in0(1'b0), .in1(pchold), .out(PC_Hold), .sel(Enable));
  Multiplexer #(.width(3), .enable("false")) multiplexer_4 (.in0(3'b000), .in1(rt), .out(Rd), .sel(Enable));
  Multiplexer #(.width(3), .enable("false")) multiplexer_5 (.in0(3'b000), .in1(rt), .out(Rm), .sel(Enable));
  Multiplexer #(.enable("false")) multiplexer_6 (.in0(1'b0), .in1(store_t), .out(Store), .sel(Enable));

  // Other names for the same wires on the sheet: clock = Clk; i[15:0] = Instruction; load_t = Instruction[11];
  //   sp[31:0] = Stack_Pointer

  // Notes on the sheet:
  //   Delay load and hold PC for 1 cycle for the RAM to send out requested data 
endmodule

module SP_Address (
  input  Enable,
  input  [31:0] Stack_Pointer,
  input  [15:0] Instruction,
  output Write_Enable,
  output [31:0] New_Stack_Pointer
);

  wire [6:0] bitselector_1_out;
  wire [31:0] adder_1_out, bit_extender_1_out, multiplexer_1_out, subtractor_1_out;

  assign bit_extender_1_out = {{25{1'b0}}, bitselector_1_out};  // Bit_Extender bit_extender_1
  BitSelector #(.width(16), .group(7)) bitselector_1 (.in(Instruction), .out(bitselector_1_out), .sel(2'b00));
  Adder #(.width(32)) adder_1 (.a(Stack_Pointer), .b(bit_extender_1_out), .out(adder_1_out));  // open: cin, cout
  Subtractor #(.width(32)) subtractor_1 (
    .a(Stack_Pointer), .b(bit_extender_1_out), .out(subtractor_1_out));  // open: bin, bout
  Multiplexer #(.width(32), .enable("false")) multiplexer_1 (
    .in0(adder_1_out), .in1(subtractor_1_out), .out(multiplexer_1_out), .sel(Instruction[7]));
  Multiplexer #(.width(32), .enable("false")) multiplexer_2 (
    .in0({32{1'b0}}), .in1(multiplexer_1_out), .out(New_Stack_Pointer), .sel(Enable));

  assign Write_Enable = Enable;

  // Other names for the same wires on the sheet: e7 = Instruction[7]; SP[31:0] = Stack_Pointer

  // Notes on the sheet:
  //   Pull output low on Enable = 0
endmodule

module Flags_APSR (
  input  [3:0] Flags_In,
  input  [3:0] Update_Mask,
  input  Clk,
  input  Rst,
  output [3:0] Flags_Out
);

  wire [3:0] and_1_out, and_2_out, not_1_out, or_1_out;

  assign and_1_out = Flags_In & Update_Mask;  // AND_Gate and_1, 4 bits wide
  assign not_1_out = ~Update_Mask;  // NOT_Gate not_1, 4 bits wide
  assign and_2_out = not_1_out & Flags_Out;  // AND_Gate and_2, 4 bits wide
  assign or_1_out = and_1_out | and_2_out;  // OR_Gate or_1, 4 bits wide
  Register #(.width(4)) register_1 (.D(or_1_out), .clk(Clk), .Q(Flags_Out), .clr(Rst));  // open: en
endmodule

module add_subR (
  input  e10,
  input  e11,
  input  e12,
  output s
);

  wire not_1_out;

  not not_1 (not_1_out, e10);
  and and_1 (s, not_1_out, e11, e12);
endmodule

module shi_ft (
  input  e11,
  input  e12,
  input  e13,
  output s
);

  wire and_1_out, and_2_out, not_1_out, not_2_out, not_3_out, not_4_out;

  not not_1 (not_1_out, e11);
  not not_2 (not_2_out, e13);
  not not_3 (not_3_out, e12);
  not not_4 (not_4_out, e13);
  and and_1 (and_1_out, not_1_out, not_2_out);
  and and_2 (and_2_out, not_3_out, not_4_out);
  or or_1 (s, and_1_out, and_2_out);
endmodule

module addsub_I (
  input  e10,
  input  e11,
  input  e12,
  output s
);

  and and_1 (s, e10, e11, e12);
endmodule

module MOV (
  input  e11,
  input  e12,
  input  e13,
  output s
);

  wire not_1_out, not_2_out;

  not not_1 (not_1_out, e11);
  not not_2 (not_2_out, e12);
  and and_1 (s, not_1_out, not_2_out, e13);
endmodule

module SUB (
  input  e13,
  input  e12,
  input  e11,
  input  e9,
  output s
);

  wire not_1_out;

  not not_1 (not_1_out, e13);
  and and_1 (s, not_1_out, e12, e11, e9);
endmodule
