// Logisim project TP1.circ as structural Verilog: 2 circuits, main circuit main
module main (
);

  wire afficheur_1_a, afficheur_1_b, afficheur_1_c, afficheur_1_d, afficheur_1_e, afficheur_1_f,
       afficheur_1_g, afficheur_2_a, afficheur_2_b, afficheur_2_c, afficheur_2_d, afficheur_2_e,
       afficheur_2_f, afficheur_2_g, clock_1_out, n7404_1_pin2, n7404_1_pin12;
  wire [7:0] n7404_1_pin1;

  _7404 u_7404_1 (
    .pin1(n7404_1_pin1[0]), .pin2(n7404_1_pin2), .pin13(n7404_1_pin2), .pin12(n7404_1_pin12));  // open: pin3, pin4, pin5, pin6, pin11, pin10, pin9, pin8
  // Probe on n7404_1_pin1
  Counter counter_1 (.clk(clock_1_out), .Q(n7404_1_pin1));  // open: clr, load, up, count, D, carry
  Clock clock_1 (.out(clock_1_out));
  Afficheur afficheur_1 (
    .e0(n7404_1_pin1[7]), .e1(n7404_1_pin1[6]), .e2(n7404_1_pin1[5]), .e3(n7404_1_pin1[4]),
    .a(afficheur_1_a), .b(afficheur_1_b), .c(afficheur_1_c), .d(afficheur_1_d), .e(afficheur_1_e),
    .f(afficheur_1_f), .g(afficheur_1_g));
  Afficheur afficheur_2 (
    .e0(n7404_1_pin1[3]), .e1(n7404_1_pin1[2]), .e2(n7404_1_pin1[1]), .e3(n7404_1_pin12), .a(afficheur_2_a),
    .b(afficheur_2_b), .c(afficheur_2_c), .d(afficheur_2_d), .e(afficheur_2_e), .f(afficheur_2_f),
    .g(afficheur_2_g));
  _7_Segment_Display u_7_segment_display_1 (
    .g(afficheur_1_g), .f(afficheur_1_f), .a(afficheur_1_a), .b(afficheur_1_b), .e(afficheur_1_e),
    .d(afficheur_1_d), .c(afficheur_1_c));  // open: dp
  _7_Segment_Display u_7_segment_display_2 (
    .g(afficheur_2_g), .f(afficheur_2_f), .a(afficheur_2_a), .b(afficheur_2_b), .e(afficheur_2_e),
    .d(afficheur_2_d), .c(afficheur_2_c));  // open: dp
endmodule

module Afficheur (
  input  e0,
  input  e1,
  input  e2,
  input  e3,
  output a,
  output b,
  output c,
  output d,
  output e,
  output f,
  output g
);

  wire and_1_out, and_2_out, and_3_out, and_4_out, and_5_out, and_6_out, and_7_out, and_8_out, and_9_out,
       and_10_out, and_11_out, and_12_out, and_13_out, and_14_out, and_15_out, and_16_out, and_17_out,
       and_18_out, and_19_out, and_20_out, and_21_out, and_22_out, and_23_out, and_24_out, and_25_out,
       and_26_out, and_27_out, and_28_out, and_29_out, and_30_out, and_31_out, and_32_out, and_33_out,
       and_34_out, and_35_out, not_1_out, not_2_out, not_3_out, not_4_out, not_5_out, not_6_out, not_7_out,
       not_8_out, not_9_out, not_10_out, not_11_out, not_12_out, not_13_out, not_14_out, not_15_out,
       not_16_out, not_17_out, not_18_out, not_19_out, not_20_out, not_21_out, not_22_out, not_23_out,
       not_24_out, not_25_out, not_26_out, not_27_out, not_28_out, not_29_out, not_30_out, not_31_out,
       not_32_out, not_33_out, not_34_out, not_35_out, not_36_out, not_37_out, not_38_out, not_39_out,
       not_40_out, not_41_out, not_42_out, not_43_out;

  not not_1 (not_1_out, e1);
  not not_2 (not_2_out, e3);
  not not_3 (not_3_out, e0);
  not not_4 (not_4_out, e0);
  not not_5 (not_5_out, e1);
  not not_6 (not_6_out, e2);
  not not_7 (not_7_out, e3);
  not not_8 (not_8_out, e0);
  not not_9 (not_9_out, e1);
  not not_10 (not_10_out, e0);
  not not_11 (not_11_out, e2);
  not not_12 (not_12_out, e3);
  not not_13 (not_13_out, e1);
  not not_14 (not_14_out, e3);
  not not_15 (not_15_out, e0);
  not not_16 (not_16_out, e2);
  not not_17 (not_17_out, e0);
  not not_18 (not_18_out, e2);
  not not_19 (not_19_out, e0);
  not not_20 (not_20_out, e2);
  not not_21 (not_21_out, e0);
  not not_22 (not_22_out, e1);
  not not_23 (not_23_out, e0);
  not not_24 (not_24_out, e1);
  not not_25 (not_25_out, e3);
  not not_26 (not_26_out, e1);
  not not_27 (not_27_out, e2);
  not not_28 (not_28_out, e3);
  not not_29 (not_29_out, e2);
  not not_30 (not_30_out, e1);
  not not_31 (not_31_out, e3);
  not not_32 (not_32_out, e3);
  not not_33 (not_33_out, e2);
  not not_34 (not_34_out, e3);
  not not_35 (not_35_out, e0);
  not not_36 (not_36_out, e2);
  not not_37 (not_37_out, e3);
  not not_38 (not_38_out, e1);
  not not_39 (not_39_out, e1);
  not not_40 (not_40_out, e3);
  not not_41 (not_41_out, e0);
  not not_42 (not_42_out, e2);
  not not_43 (not_43_out, e1);
  and and_1 (and_1_out, not_1_out, not_2_out);
  and and_2 (and_2_out, not_3_out, e2);
  and and_3 (and_3_out, not_4_out, e1, e3);
  and and_4 (and_4_out, e1, e2);
  and and_5 (and_5_out, e0, not_5_out, not_6_out);
  and and_6 (and_6_out, e0, not_7_out);
  and and_7 (and_7_out, not_8_out, not_9_out);
  and and_8 (and_8_out, not_10_out, not_11_out, not_12_out);
  and and_9 (and_9_out, not_13_out, not_14_out);
  and and_10 (and_10_out, not_15_out, e2, e3);
  and and_11 (and_11_out, e0, not_16_out, e3);
  and and_12 (and_12_out, not_17_out, not_18_out);
  and and_13 (and_13_out, not_19_out, e3);
  and and_14 (and_14_out, not_20_out, e3);
  and and_15 (and_15_out, not_21_out, e1);
  and and_16 (and_16_out, e0, not_22_out);
  and and_17 (and_17_out, not_23_out, not_24_out, not_25_out);
  and and_18 (and_18_out, not_26_out, e2, e3);
  and and_19 (and_19_out, e1, not_27_out, e3);
  and and_20 (and_20_out, e1, e2, not_28_out);
  and and_21 (and_21_out, e0, not_29_out);
  and and_22 (and_22_out, not_30_out, not_31_out);
  and and_23 (and_23_out, e2, not_32_out);
  and and_24 (and_24_out, e0, e2);
  and and_25 (and_25_out, e0, e1);
  and and_26 (and_26_out, not_33_out, not_34_out);
  and and_27 (and_27_out, not_35_out, e1, not_36_out);
  and and_28 (and_28_out, e1, not_37_out);
  and and_29 (and_29_out, e0, not_38_out);
  and and_30 (and_30_out, e0, e2);
  and and_31 (and_31_out, not_39_out, e2);
  and and_32 (and_32_out, e2, not_40_out);
  and and_33 (and_33_out, not_41_out, e1, not_42_out);
  and and_34 (and_34_out, e0, not_43_out);
  and and_35 (and_35_out, e0, e3);
  or or_1 (a, and_1_out, and_2_out, and_3_out, and_4_out, and_5_out, and_6_out);
  or or_2 (b, and_7_out, and_8_out, and_9_out, and_10_out, and_11_out);
  or or_3 (c, and_12_out, and_13_out, and_14_out, and_15_out, and_16_out);
  or or_4 (d, and_17_out, and_18_out, and_19_out, and_20_out, and_21_out);
  or or_5 (e, and_22_out, and_23_out, and_24_out, and_25_out);
  or or_6 (f, and_26_out, and_27_out, and_28_out, and_29_out, and_30_out);
  or or_7 (g, and_31_out, and_32_out, and_33_out, and_34_out, and_35_out);
  _7_Segment_Display u_7_segment_display_1 (.g(g), .f(f), .a(a), .b(b), .e(e), .d(d), .c(c));  // open: dp
endmodule
